# Fritzing sketch Buzzer2 (saved by Fritzing 0.9.10b)
circuit board: 3.93405cm x 1.90014cm
breadboards: 1

parts:
  Atmega328P-AU = ATmega328 [package=tqfp]
  MS5611 = MPL3115A2 [package=lga8]
  BC818-16 = NPN-Transistor [package="SOT-23 [SMD]"]
  10K = Resistor [tolerance=±5% resistance=10k package="0603 [SMD]"]
  10K_2 = Resistor [tolerance=±5% resistance=10k package="0603 [SMD]"]
  KSSGJ44B20 = Piezo Speaker
  +_-_r_t = PIC-ICSP-Mini [package=pic-icsp-mini]
  100nF = Capacitor [package=1210]
  R1 = Resistor [tolerance=±5% resistance=1k package="0603 [SMD]"]

nets:
  GND: Atmega328P-AU.GND, Atmega328P-AU.AGND, MS5611.GND, MS5611.SCB, MS5611.INT2, KSSGJ44B20.pin2, +_-_r_t.GND, 100nF.2
  VCC: Atmega328P-AU.VCC, Atmega328P-AU.AVCC, MS5611.VDD, MS5611.PS, BC818-16.1, 10K.Pin_0, 10K_2.Pin_0, +_-_r_t.VCC, 100nF.1
  N1: Atmega328P-AU.PB1(OC1A), BC818-16.0
  N2: Atmega328P-AU.PC4(ADC4_SDA), MS5611.SDA, 10K.Pin_1
  N3: Atmega328P-AU.PC5(ADC5_SCL), MS5611.SCL, 10K_2.Pin_1
  N4: Atmega328P-AU.PC6(_RESET), +_-_r_t.RESET, R1.Pin_0
  N5: Atmega328P-AU.PD0(RXD), +_-_r_t.RX
  N6: Atmega328P-AU.PD1(TXD), +_-_r_t.TX
  N7: Atmega328P-AU.PD2(INT0), R1.Pin_1
  N8: BC818-16.2, KSSGJ44B20.pin1

custom parts:
  MPL3115A2: Altimeter/Pressure Sensor, I2C, 1.95V-3.6V supply, 50 to 110kPa
  Piezo Speaker: Piezo
  PIC-ICSP-Mini: PIC-ICSP-Mini Miniature 5-pin connection for temporary programming of PICs. Use this device in your design to save space. Program the PIC with this adapter Spark Fun Electronics SKU : BOB-00194
